// Logisim project JUNIN ProcessadorFinal.circ as structural Verilog: 8 circuits, main circuit Processador
// R2V
module Processador (
  input  in_1,
  input  Clear,
  output [1:0] out_3,
  output [15:0] out_4,
  output [15:0] code,
  output [2:0] OP,
  output [3:0] RA,
  output [3:0] RB,
  output [3:0] Salvar_Reg,
  output [15:0] Valor_RA,
  output [15:0] Valor_RB,
  output [15:0] Entrada_ULA_1,
  output [15:0] Entrada_ULA_2,
  output [15:0] Saida_da_ULA,
  output [15:0] Entrada_de_Dado_Memoria,
  output [15:0] Para_Reg,
  output [15:0] DM,
  output [15:0] I,
  output [3:0] out_19
);

  wire and_1_out, Clock, uc_1_branch, uc_1_jump, uc_1_memread, uc_1_memtoreg, uc_1_memwrite, uc_1_regwrite,
       uc_1_ulasrc, ula_1_zero;
  wire [15:0] adder_1_out, multiplexer_3_out, ram_1_data, register_1_q, somador_1_1_out_2;

  Clock u_Clock (.out(Clock));
  Register #(.width(16)) register_1 (.D(DM), .Q(register_1_q), .clk(Clock), .clr(Clear));  // open: en
  ROM #(.addrWidth(16), .dataWidth(16)) rom_1 (.addr(register_1_q), .data(code));  // open: sel
  Somador_1 somador_1_1 (.in_1(register_1_q), .out_2(somador_1_1_out_2));
  Multiplexer #(.width(4), .enable("false")) multiplexer_1 (
    .in0(code[8:5]), .in1(code[4:1]), .out(out_19), .sel(uc_1_memtoreg));
  BR br_1 (
    .Valor_a_atribuir(Para_Reg), .Clock(Clock), .R1(Entrada_ULA_1), .R2(Entrada_de_Dado_Memoria),
    .Clear(Clear), .\Endereço_1 (code[12:9]), .\Endereço_2 (code[8:5]), .Enable(uc_1_regwrite),
    .Write_Register(out_19));
  UC uc_1 (
    .Enable(1'b1), .RegWrite(uc_1_regwrite), .MemRead(uc_1_memread), .MemWrite(uc_1_memwrite),
    .MemToReg(uc_1_memtoreg), .Branch(uc_1_branch), .Jump(uc_1_jump), .ULAOP(out_3), .in_2(code[15:13]),
    .ULASrc(uc_1_ulasrc));
  Multiplexer #(.width(16), .enable("false")) multiplexer_2 (
    .in0(Entrada_de_Dado_Memoria), .in1({{11{1'b0}}, code[4:0]}), .out(Entrada_ULA_2), .sel(uc_1_ulasrc));
  Multiplexer #(.width(16), .enable("false")) multiplexer_3 (
    .in0(somador_1_1_out_2), .in1({somador_1_1_out_2[15:13], code[12:0]}), .out(multiplexer_3_out),
    .sel(uc_1_jump));
  ULA ula_1 (
    .\Saída (out_4), .Zero(ula_1_zero), .EntA(Entrada_ULA_1), .EntB(Entrada_ULA_2), .ULAOP(out_3));  // open: in_4
  Adder #(.width(16)) adder_1 (
    .a(multiplexer_3_out), .b({{11{1'b0}}, code[4:0]}), .out(adder_1_out));  // open: cin, cout
  and and_1 (and_1_out, uc_1_branch, ula_1_zero);
  Multiplexer #(.width(16), .enable("false")) multiplexer_4 (
    .in0(multiplexer_3_out), .in1(adder_1_out), .out(DM), .sel(and_1_out));
  RAM #(.addrWidth(16), .dataWidth(16), .bus("separate")) ram_1 (
    .addr(out_4), .din(Entrada_de_Dado_Memoria), .data(ram_1_data), .str(uc_1_memwrite), .clk(Clock),
    .ld(uc_1_memread), .clr(in_1));  // open: sel
  Multiplexer #(.width(16), .enable("false")) multiplexer_5 (
    .in0(out_4), .in1(ram_1_data), .out(Para_Reg), .sel(uc_1_memtoreg));

  assign I = {{11{1'b0}}, code[4:0]};
  assign OP = code[15:13];
  assign RA = code[12:9];
  assign RB = code[8:5];
  assign Saida_da_ULA = out_4;
  assign Salvar_Reg = code[4:1];
  assign Valor_RA = Entrada_ULA_1;
  assign Valor_RB = Entrada_de_Dado_Memoria;

  // Other names for the same wires on the sheet: Imediato[4:0] = code[4:0]; DeslocMemoria[15:0] = DM;
  //   R3[3:0] = code[4:1]; R1[3:0] = code[12:9]; R2[3:0] = code[8:5]; MEMENTRADA[15:0] = Entrada_de_Dado_Memoria;
  //   R2V[15:0] = Entrada_de_Dado_Memoria; ToRegister[15:0] = Para_Reg; R1V[15:0] = Entrada_ULA_1;
  //   ULA1[15:0] = Entrada_ULA_1; ULA2[15:0] = Entrada_ULA_2; ULAS[15:0] = out_4; WR[3:0] = out_19

  // Notes on the sheet:
  //   contents of rom_1 (hex, n*v repeats v):
  //   242 a0 4024 0 100 0 10 100 10 100 100 1110
  //   beq
  //   beq
  //   j
endmodule

module Registrador_16bits (
  input  Clock,
  input  Clear,
  input  [15:0] Dado,
  output [15:0] \Saída 
);

  D_Flip_Flop d_ff_1 (.clk(Clock), .D(Dado[15]), .Q(\Saída [15]), .reset(Clear));  // open: Qn, preset, en
  D_Flip_Flop d_ff_2 (.clk(Clock), .D(Dado[14]), .Q(\Saída [14]), .reset(Clear));  // open: Qn, preset, en
  D_Flip_Flop d_ff_3 (.clk(Clock), .D(Dado[13]), .Q(\Saída [13]), .reset(Clear));  // open: Qn, preset, en
  D_Flip_Flop d_ff_4 (.clk(Clock), .D(Dado[12]), .Q(\Saída [12]), .reset(Clear));  // open: Qn, preset, en
  D_Flip_Flop d_ff_5 (.clk(Clock), .D(Dado[11]), .Q(\Saída [11]), .reset(Clear));  // open: Qn, preset, en
  D_Flip_Flop d_ff_6 (.clk(Clock), .D(Dado[10]), .Q(\Saída [10]), .reset(Clear));  // open: Qn, preset, en
  D_Flip_Flop d_ff_7 (.clk(Clock), .D(Dado[9]), .Q(\Saída [9]), .reset(Clear));  // open: Qn, preset, en
  D_Flip_Flop d_ff_8 (.clk(Clock), .D(Dado[8]), .Q(\Saída [8]), .reset(Clear));  // open: Qn, preset, en
  D_Flip_Flop d_ff_9 (.clk(Clock), .D(Dado[7]), .Q(\Saída [7]), .reset(Clear));  // open: Qn, preset, en
  D_Flip_Flop d_ff_10 (.clk(Clock), .D(Dado[6]), .Q(\Saída [6]), .reset(Clear));  // open: Qn, preset, en
  D_Flip_Flop d_ff_11 (.clk(Clock), .D(Dado[5]), .Q(\Saída [5]), .reset(Clear));  // open: Qn, preset, en
  D_Flip_Flop d_ff_12 (.clk(Clock), .D(Dado[4]), .Q(\Saída [4]), .reset(Clear));  // open: Qn, preset, en
  D_Flip_Flop d_ff_13 (.clk(Clock), .D(Dado[3]), .Q(\Saída [3]), .reset(Clear));  // open: Qn, preset, en
  D_Flip_Flop d_ff_14 (.clk(Clock), .D(Dado[2]), .Q(\Saída [2]), .reset(Clear));  // open: Qn, preset, en
  D_Flip_Flop d_ff_15 (.clk(Clock), .D(Dado[1]), .Q(\Saída [1]), .reset(Clear));  // open: Qn, preset, en
  D_Flip_Flop d_ff_16 (.clk(Clock), .D(Dado[0]), .Q(\Saída [0]), .reset(Clear));  // open: Qn, preset, en
endmodule

module BR (
  input  Clear,
  input  [15:0] Valor_a_atribuir,
  input  Clock,
  input  [3:0] \Endereço_1 ,
  input  Enable,
  input  [3:0] Write_Register,
  input  [3:0] \Endereço_2 ,
  output [15:0] R1,
  output [15:0] R2
);

  wire demultiplexer_1_out0, demultiplexer_1_out1, demultiplexer_1_out2, demultiplexer_1_out3,
       demultiplexer_1_out4, demultiplexer_1_out5, demultiplexer_1_out6, demultiplexer_1_out7,
       demultiplexer_1_out8, demultiplexer_1_out9, demultiplexer_1_out10, demultiplexer_1_out11,
       demultiplexer_1_out12, demultiplexer_1_out13, demultiplexer_1_out14, demultiplexer_1_out15;
  wire [15:0] \_0000_saída , \_0001_saída , \_0010_saída , \_0011_saída , \_0100_saída , \_0101_saída ,
       \_0110_saída , \_0111_saída , \_1000_saída , \_1001_saída , \_1010_saída , \_1011_saída ,
       \_1100_saída , \_1101_saída , \_1110_saída , \_1111_saída ;

  Demultiplexer #(.select(4)) demultiplexer_1 (
    .out0(demultiplexer_1_out0), .out1(demultiplexer_1_out1), .out2(demultiplexer_1_out2),
    .out3(demultiplexer_1_out3), .out4(demultiplexer_1_out4), .out5(demultiplexer_1_out5),
    .out6(demultiplexer_1_out6), .out7(demultiplexer_1_out7), .out8(demultiplexer_1_out8),
    .out9(demultiplexer_1_out9), .out10(demultiplexer_1_out10), .out11(demultiplexer_1_out11),
    .out12(demultiplexer_1_out12), .out13(demultiplexer_1_out13), .out14(demultiplexer_1_out14),
    .out15(demultiplexer_1_out15), .in(Clock), .sel(Write_Register), .en(Enable));
  Registrador_16bits _0000 (
    .Clock(demultiplexer_1_out0), .Clear(Clear), .Dado(Valor_a_atribuir), .\Saída (\_0000_saída ));
  Registrador_16bits _0001 (
    .Clock(demultiplexer_1_out1), .Clear(Clear), .Dado(Valor_a_atribuir), .\Saída (\_0001_saída ));
  Registrador_16bits _0010 (
    .Clock(demultiplexer_1_out2), .Clear(Clear), .Dado(Valor_a_atribuir), .\Saída (\_0010_saída ));
  Registrador_16bits _0011 (
    .Clock(demultiplexer_1_out3), .Clear(Clear), .Dado(Valor_a_atribuir), .\Saída (\_0011_saída ));
  Registrador_16bits _0100 (
    .Clock(demultiplexer_1_out4), .Clear(Clear), .Dado(Valor_a_atribuir), .\Saída (\_0100_saída ));
  Registrador_16bits _0110 (
    .Clock(demultiplexer_1_out6), .Clear(Clear), .Dado(Valor_a_atribuir), .\Saída (\_0110_saída ));
  Registrador_16bits _0111 (
    .Clock(demultiplexer_1_out7), .Clear(Clear), .Dado(Valor_a_atribuir), .\Saída (\_0111_saída ));
  Registrador_16bits _1000 (
    .Clock(demultiplexer_1_out8), .Clear(Clear), .Dado(Valor_a_atribuir), .\Saída (\_1000_saída ));
  Registrador_16bits _1001 (
    .Clock(demultiplexer_1_out9), .Clear(Clear), .Dado(Valor_a_atribuir), .\Saída (\_1001_saída ));
  Registrador_16bits _1010 (
    .Clock(demultiplexer_1_out10), .Clear(Clear), .Dado(Valor_a_atribuir), .\Saída (\_1010_saída ));
  Registrador_16bits _1011 (
    .Clock(demultiplexer_1_out11), .Clear(Clear), .Dado(Valor_a_atribuir), .\Saída (\_1011_saída ));
  Registrador_16bits _1100 (
    .Clock(demultiplexer_1_out12), .Clear(Clear), .Dado(Valor_a_atribuir), .\Saída (\_1100_saída ));
  Registrador_16bits _1101 (
    .Clock(demultiplexer_1_out13), .Clear(Clear), .Dado(Valor_a_atribuir), .\Saída (\_1101_saída ));
  Registrador_16bits _1110 (
    .Clock(demultiplexer_1_out14), .Clear(Clear), .Dado(Valor_a_atribuir), .\Saída (\_1110_saída ));
  Registrador_16bits _1111 (
    .Clock(demultiplexer_1_out15), .Clear(Clear), .Dado(Valor_a_atribuir), .\Saída (\_1111_saída ));
  Registrador_16bits _0101 (
    .Clock(demultiplexer_1_out5), .Clear(Clear), .Dado(Valor_a_atribuir), .\Saída (\_0101_saída ));
  Multiplexer #(.select(4), .width(16), .enable("false")) multiplexer_1 (
    .in0(\_0000_saída ), .in1(\_0001_saída ), .in2(\_0010_saída ), .in3(\_0011_saída ), .in4(\_0100_saída ),
    .in5(\_0101_saída ), .in6(\_0110_saída ), .in7(\_0111_saída ), .in8(\_1000_saída ), .in9(\_1001_saída ),
    .in10(\_1010_saída ), .in11(\_1011_saída ), .in12(\_1100_saída ), .in13(\_1101_saída ),
    .in14(\_1110_saída ), .in15(\_1111_saída ), .out(R1), .sel(\Endereço_1 ));
  Multiplexer #(.select(4), .width(16), .enable("false")) multiplexer_2 (
    .in0(\_0000_saída ), .in1(\_0001_saída ), .in2(\_0010_saída ), .in3(\_0011_saída ), .in4(\_0100_saída ),
    .in5(\_0101_saída ), .in6(\_0110_saída ), .in7(\_0111_saída ), .in8(\_1000_saída ), .in9(\_1001_saída ),
    .in10(\_1010_saída ), .in11(\_1011_saída ), .in12(\_1100_saída ), .in13(\_1101_saída ),
    .in14(\_1110_saída ), .in15(\_1111_saída ), .out(R2), .sel(\Endereço_2 ));
endmodule

module UC (
  input  Enable,
  input  [2:0] in_2,
  output RegWrite,
  output MemRead,
  output MemWrite,
  output MemToReg,
  output Branch,
  output Jump,
  output ULASrc,
  output [1:0] ULAOP
);

  wire demultiplexer_1_out2, demultiplexer_1_out3;

  Demultiplexer #(.select(3), .enable("false")) demultiplexer_1 (
    .out0(MemRead), .out1(MemWrite), .out2(demultiplexer_1_out2), .out3(demultiplexer_1_out3), .out4(Branch),
    .out5(Jump), .in(Enable), .sel(in_2));  // open: out6, out7
  or or_1 (ULASrc, MemRead, MemWrite);
  or or_2 (RegWrite, MemRead, demultiplexer_1_out2, demultiplexer_1_out3);
  Multiplexer #(.select(3), .width(2), .enable("false")) multiplexer_1 (
    .in0(2'b10), .in1(2'b10), .in2(2'b10), .in3(2'b11), .in4(2'b11), .out(ULAOP), .sel(in_2));  // open: in5, in6, in7

  assign MemToReg = MemRead;
endmodule

module ULA (
  input  [15:0] EntA,
  input  [15:0] EntB,
  input  [1:0] ULAOP,
  input  in_4,
  output [15:0] \Saída ,
  output Zero
);

  wire subtractor_1_bout;
  wire [15:0] adder_1_out, and_1_out, or_1_out, subtractor_1_out;

  assign and_1_out = EntA & EntB;  // AND_Gate and_1, 16 bits wide
  assign or_1_out = EntA | EntB;  // OR_Gate or_1, 16 bits wide
  Adder #(.width(16)) adder_1 (.a(EntA), .b(EntB), .out(adder_1_out));  // open: cin, cout
  Subtractor #(.width(16)) subtractor_1 (
    .a(EntA), .b(EntB), .out(subtractor_1_out), .bout(subtractor_1_bout));  // open: bin
  and and_2 (Zero, ~subtractor_1_bout, ~\Saída [15], ~\Saída [14], ~\Saída [13], ~\Saída [12], ~\Saída [11], ~\Saída [10], ~\Saída [9], ~\Saída [8], ~\Saída [7], ~\Saída [6], ~\Saída [5], ~\Saída [4], ~\Saída [3], ~\Saída [2], ~\Saída [1], ~\Saída [0]);  // AND_Gate
  Multiplexer #(.select(2), .width(16)) multiplexer_1 (
    .in0(and_1_out), .in1(or_1_out), .in2(adder_1_out), .in3(subtractor_1_out), .out(\Saída ), .sel(ULAOP),
    .en(in_4));
endmodule

module Somador_1 (
  input  [15:0] in_1,
  output [15:0] out_2
);

  Adder #(.width(16)) adder_1 (.a(in_1), .b(16'h1), .out(out_2));  // open: cin, cout
endmodule

module Mux_2x1 (
  input  \Endereço ,
  input  [7:0] _0,
  input  [7:0] _1,
  output [7:0] \Saída 
);

  wire and_1_out, and_2_out, and_3_out, and_4_out, and_5_out, and_6_out, and_7_out, and_8_out, and_9_out,
       and_10_out, and_11_out, and_12_out, and_13_out, and_14_out, and_15_out, and_16_out;

  and and_1 (and_1_out, ~\Endereço , _0[0]);  // AND_Gate
  and and_2 (and_2_out, \Endereço , _1[0]);
  and and_3 (and_3_out, ~\Endereço , _0[1]);  // AND_Gate
  and and_4 (and_4_out, \Endereço , _1[1]);
  and and_5 (and_5_out, ~\Endereço , _0[2]);  // AND_Gate
  and and_6 (and_6_out, \Endereço , _1[2]);
  and and_7 (and_7_out, ~\Endereço , _0[3]);  // AND_Gate
  and and_8 (and_8_out, \Endereço , _1[3]);
  and and_9 (and_9_out, ~\Endereço , _0[4]);  // AND_Gate
  and and_10 (and_10_out, \Endereço , _1[4]);
  and and_11 (and_11_out, ~\Endereço , _0[5]);  // AND_Gate
  and and_12 (and_12_out, \Endereço , _1[5]);
  and and_13 (and_13_out, ~\Endereço , _0[6]);  // AND_Gate
  and and_14 (and_14_out, \Endereço , _1[6]);
  and and_15 (and_15_out, ~\Endereço , _0[7]);  // AND_Gate
  and and_16 (and_16_out, \Endereço , _1[7]);
  or or_1 (\Saída [0], and_1_out, and_2_out);
  or or_2 (\Saída [1], and_3_out, and_4_out);
  or or_3 (\Saída [2], and_5_out, and_6_out);
  or or_4 (\Saída [3], and_7_out, and_8_out);
  or or_5 (\Saída [4], and_9_out, and_10_out);
  or or_6 (\Saída [5], and_11_out, and_12_out);
  or or_7 (\Saída [6], and_13_out, and_14_out);
  or or_8 (\Saída [7], and_15_out, and_16_out);
endmodule

module Processador2 (
  input  Clear
);

  wire and_1_out, br_1_p5, br_1_p8, Clock, uc_1_branch, uc_1_jump, uc_1_memread, uc_1_memtoreg,
       uc_1_memwrite, uc_1_ulasrc, ula_1_p4;
  wire [1:0] uc_1_ulaop;
  wire [7:0] adder_1_out, br_1_p4, br_1_p9, multiplexer_1_out, multiplexer_2_out, multiplexer_3_out,
       ram_1_data, register_1_q, rom_1_data, somador_1_1_p2, ula_1_p5;

  Clock u_Clock (.out(Clock));
  Register register_1 (.D(multiplexer_3_out), .Q(register_1_q), .clk(Clock), .clr(Clear));  // open: en
  ROM rom_1 (.addr(register_1_q), .data(rom_1_data));  // open: sel
  // Somador_1 somador_1_1: pin names not known; wires that end beside it: register_1_q, somador_1_1_p2
  // BR br_1: pin names not known; wires that end beside it: {rom_1_data[3], rom_1_data[4]}, {rom_1_data[1], rom_1_data[2]}, {rom_1_data[1], rom_1_data[2]}, br_1_p4, br_1_p5, Clock, Clear, br_1_p8, br_1_p9
  UC uc_1 (
    .Enable(1'b1), .RegWrite(br_1_p5), .MemRead(uc_1_memread), .MemWrite(uc_1_memwrite),
    .MemToReg(uc_1_memtoreg), .Branch(uc_1_branch), .Jump(uc_1_jump), .ULAOP(uc_1_ulaop),
    .in_2(rom_1_data[7:5]), .ULASrc(uc_1_ulasrc));
  Multiplexer #(.width(8), .enable("false")) multiplexer_1 (
    .in0(br_1_p9), .in1({{7{1'b0}}, rom_1_data[0]}), .out(multiplexer_1_out), .sel(uc_1_ulasrc));
  Multiplexer #(.width(8), .enable("false")) multiplexer_2 (
    .in0(somador_1_1_p2),
    .in1({somador_1_1_p2[7:5], rom_1_data[3], rom_1_data[4], rom_1_data[1], rom_1_data[2], rom_1_data[0]}),
    .out(multiplexer_2_out), .sel(uc_1_jump));
  // ULA ula_1: pin names not known; wires that end beside it: br_1_p8, multiplexer_1_out, uc_1_ulaop, ula_1_p4, ula_1_p5
  Adder adder_1 (.a(multiplexer_2_out), .b({{7{1'b0}}, rom_1_data[0]}), .out(adder_1_out));  // open: cin, cout
  and and_1 (and_1_out, uc_1_branch, ula_1_p4);
  Multiplexer #(.width(8), .enable("false")) multiplexer_3 (
    .in0(multiplexer_2_out), .in1(adder_1_out), .out(multiplexer_3_out), .sel(and_1_out));
  RAM #(.bus("separate")) ram_1 (
    .addr(ula_1_p5), .din(br_1_p9), .data(ram_1_data), .str(uc_1_memwrite), .clk(Clock), .ld(uc_1_memread));  // open: sel, clr
  Multiplexer #(.width(8), .enable("false")) multiplexer_4 (
    .in0(ula_1_p5), .in1(ram_1_data), .out(br_1_p4), .sel(uc_1_memtoreg));

  // Notes on the sheet:
  //   contents of rom_1 (hex, n*v repeats v):
  //   11 0 0 0 29 0 0 0 43 0 0 0 54 0 0 0 12
endmodule
